# Fritzing sketch ArduinoServoJoystick (saved by Fritzing 0.9.2b)
breadboards: 1

parts:
  Composant1 = Arduino Uno (Rev3)
  U1 = Thumb Joystick [package=joystick]
  J1 = Basic Servo
  R1 = Resistor [tolerance=±5% resistance=4.7k package=THT]
  D1 = Rectifier Diode [part_number=1N4001 package="300 mil [THT]"]  # not connected
  J2 = Basic Servo
  R2 = Resistor [tolerance=±5% resistance=4.7k package=THT]

nets:
  N1: Composant1.A0, U1.H-
  N2: Composant1.A1, U1.V-
  N3: Composant1.D9_PWM, J1.pulse, R1.Pin_1
  N4: Composant1.D13/SCK, U1.H
  N5: Composant1.D5_PWM, J2.pulse, R2.Pin_1
  N6: Composant1.5V, U1.V
  GND: Composant1.GND, U1.SEL-, J1.gnd, R1.Pin_0, J2.gnd, R2.Pin_0
  VCC: J1.vcc, J2.vcc
